# Fritzing sketch 01_sonic_distance (saved by Fritzing 0.9.3b)
breadboards: 1

parts:
  부품1 = Arduino Uno (Rev3)
  HC-SR04_Sensor_1 = HC-SR04 Ultrasonic Distance Sensor

nets:
  N1: 부품1.D11_PWM/MOSI, HC-SR04_Sensor_1.ECHO
  N2: 부품1.D12/MISO, HC-SR04_Sensor_1.TRIG
  5V: 부품1.5V, HC-SR04_Sensor_1.VCC
  GND: 부품1.GND, HC-SR04_Sensor_1.GND
