# Fritzing sketch 02_sonic_led (saved by Fritzing 0.9.3b)
breadboards: 1

parts:
  부품1 = Arduino Uno (Rev3)
  HC-SR04_Sensor_1 = HC-SR04 Ultrasonic Distance Sensor
  LED1 = LED - 5mm [color="Red (633nm)" package="5 mm [THT]"]
  LED2 = LED - 5mm [color="Yellow (595nm)" package="5 mm [THT]"]
  LED3 = LED - 5mm [color="Green (555nm)" package="5 mm [THT]"]
  R1 = Resistor [tolerance=±5% resistance=220 package=THT]
  R2 = Resistor [tolerance=±5% resistance=220 package=THT]
  R3 = Resistor [tolerance=±5% resistance=220 package=THT]

nets (from the breadboard view):
  N1: 부품1.D11_PWM/MOSI, HC-SR04_Sensor_1.TRIG
  N2: 부품1.D12/MISO, HC-SR04_Sensor_1.ECHO
  N3: 부품1.D5_PWM, LED3.anode
  N4: 부품1.D6_PWM, LED2.anode
  N5: 부품1.D7, LED1.anode
  5V: 부품1.5V, HC-SR04_Sensor_1.VCC
  GND: 부품1.GND, HC-SR04_Sensor_1.GND
  N6: LED1.cathode, R1.Pin_1
  N7: LED2.cathode, R2.Pin_1
  N8: LED3.cathode, R3.Pin_1
