# Fritzing sketch 03_sonic_piezo (saved by Fritzing 0.9.3b)
breadboards: 1

parts:
  부품1 = Arduino Uno (Rev3)
  HC-SR04_Sensor_1 = HC-SR04 Ultrasonic Distance Sensor
  J1 = Piezo Speaker

nets:
  N1: 부품1.D11_PWM/MOSI, HC-SR04_Sensor_1.TRIG
  GND: 부품1.D12/MISO, 부품1.GND, HC-SR04_Sensor_1.ECHO, HC-SR04_Sensor_1.GND, J1.pin1
  5V: 부품1.5V, HC-SR04_Sensor_1.VCC, J1.pin2
