# Fritzing sketch 04_sonic_piezo_lcd (saved by Fritzing 0.9.3b)
breadboards: 1

parts:
  부품1 = Arduino Uno (Rev3)
  HC-SR04_Sensor_1 = HC-SR04 Ultrasonic Distance Sensor
  J1 = Piezo Speaker
  LCD1 = LCD screen
  U1 = POT [package=pot_mammoth]

nets:
  N1: 부품1.D9_PWM, LCD1.E
  N2: 부품1.D10_PWM/SS, LCD1.RS
  N3: 부품1.D11_PWM/MOSI, HC-SR04_Sensor_1.TRIG
  GND: 부품1.D12/MISO, 부품1.GND, HC-SR04_Sensor_1.ECHO, HC-SR04_Sensor_1.GND, J1.pin1, LCD1.VSS, LCD1.R/W, LCD1.LED-, U1.S
  N4: 부품1.D2, LCD1.DB4
  N5: 부품1.D3_PWM, LCD1.DB5
  N6: 부품1.D4, LCD1.DB6
  N7: 부품1.D5_PWM, LCD1.DB7
  5V: 부품1.5V, HC-SR04_Sensor_1.VCC, J1.pin2, LCD1.VDD, LCD1.LED+, U1.E
  N8: LCD1.V0, U1.A
